// Logisim project lab2part32320.circ as structural Verilog: 1 circuit, main circuit main
module main (
  input  A0,
  input  A1,
  input  A2,
  input  A3,
  input  A4,
  output D0,
  output D0_2,
  output D0_3,
  output D0_4,
  output D0_5,
  output D0_6,
  output D0_7
);

  wire decoder_1_out0, decoder_1_out1, decoder_1_out2, decoder_1_out3;

  Decoder #(.select(2)) decoder_1 (
    .out0(decoder_1_out0), .out1(decoder_1_out1), .out2(decoder_1_out2), .out3(decoder_1_out3), .sel({A4, A3}));  // open: en
  Decoder #(.select(3)) decoder_2 (
    .sel({A2, A1, A0}), .en(decoder_1_out0));  // open: out0, out1, out2, out3, out4, out5, out6, out7
  Decoder #(.select(3)) decoder_3 (
    .sel({A2, A1, A0}), .en(decoder_1_out1));  // open: out0, out1, out2, out3, out4, out5, out6, out7
  Decoder #(.select(3)) decoder_4 (
    .sel({A2, A1, A0}), .en(decoder_1_out2));  // open: out0, out1, out2, out3, out4, out5, out6, out7
  Decoder #(.select(3)) decoder_5 (
    .sel({A2, A1, A0}), .en(decoder_1_out3));  // open: out0, out1, out2, out3, out4, out5, out6, out7
endmodule
